// Logisim project frisgotchi.circ as structural Verilog: 2 circuits, main circuit main
module main (
);

  wire [31:0] idle_anim_1__0, idle_anim_1_out_2, idle_anim_1_out_3, idle_anim_1_out_4, idle_anim_1_out_5,
       idle_anim_1_out_7, idle_anim_1_out_8, idle_anim_1_out_9, idle_anim_1_out_10, idle_anim_1_out_11,
       idle_anim_1_out_12, idle_anim_1_out_13, idle_anim_1_out_14, idle_anim_1_out_15, idle_anim_1_out_16,
       idle_anim_1_out_17, idle_anim_1_out_18, idle_anim_1_out_19, idle_anim_1_out_20, idle_anim_1_out_21,
       idle_anim_1_out_22, idle_anim_1_out_23, idle_anim_1_out_24, idle_anim_1_out_25, idle_anim_1_out_26,
       idle_anim_1_out_27, idle_anim_1_out_28, idle_anim_1_out_29, idle_anim_1_out_30, idle_anim_1_out_31,
       idle_anim_1_out_32, idle_anim_1_out_33;

  DotMatrix #(.matrixcols(32), .matrixrows(32)) dotmatrix_1 (
    .col0(idle_anim_1_out_2), .col1(idle_anim_1_out_3), .col2(idle_anim_1_out_4), .col3(idle_anim_1_out_5),
    .col4(idle_anim_1__0), .col5(idle_anim_1_out_7), .col6(idle_anim_1_out_8), .col7(idle_anim_1_out_9),
    .col8(idle_anim_1_out_10), .col9(idle_anim_1_out_11), .col10(idle_anim_1_out_12),
    .col11(idle_anim_1_out_13), .col12(idle_anim_1_out_14), .col13(idle_anim_1_out_15),
    .col14(idle_anim_1_out_16), .col15(idle_anim_1_out_17), .col16(idle_anim_1_out_18),
    .col17(idle_anim_1_out_19), .col18(idle_anim_1_out_20), .col19(idle_anim_1_out_21),
    .col20(idle_anim_1_out_22), .col21(idle_anim_1_out_23), .col22(idle_anim_1_out_24),
    .col23(idle_anim_1_out_25), .col24(idle_anim_1_out_26), .col25(idle_anim_1_out_27),
    .col26(idle_anim_1_out_28), .col27(idle_anim_1_out_29), .col28(idle_anim_1_out_30),
    .col29(idle_anim_1_out_31), .col30(idle_anim_1_out_32), .col31(idle_anim_1_out_33));
  idle_anim idle_anim_1 (
    .out_2(idle_anim_1_out_2), .out_3(idle_anim_1_out_3), .out_4(idle_anim_1_out_4),
    .out_5(idle_anim_1_out_5), ._0(idle_anim_1__0), .out_7(idle_anim_1_out_7), .out_8(idle_anim_1_out_8),
    .out_9(idle_anim_1_out_9), .out_10(idle_anim_1_out_10), .out_11(idle_anim_1_out_11),
    .out_12(idle_anim_1_out_12), .out_13(idle_anim_1_out_13), .out_14(idle_anim_1_out_14),
    .out_15(idle_anim_1_out_15), .out_16(idle_anim_1_out_16), .out_17(idle_anim_1_out_17),
    .out_18(idle_anim_1_out_18), .out_19(idle_anim_1_out_19), .out_20(idle_anim_1_out_20),
    .out_21(idle_anim_1_out_21), .out_22(idle_anim_1_out_22), .out_23(idle_anim_1_out_23),
    .out_24(idle_anim_1_out_24), .out_25(idle_anim_1_out_25), .out_26(idle_anim_1_out_26),
    .out_27(idle_anim_1_out_27), .out_28(idle_anim_1_out_28), .out_29(idle_anim_1_out_29),
    .out_30(idle_anim_1_out_30), .out_31(idle_anim_1_out_31), .out_32(idle_anim_1_out_32),
    .out_33(idle_anim_1_out_33));  // open: in_1
endmodule

module idle_anim (
  input  in_1,
  output [31:0] out_2,
  output [31:0] out_3,
  output [31:0] out_4,
  output [31:0] out_5,
  output [31:0] _0,
  output [31:0] out_7,
  output [31:0] out_8,
  output [31:0] out_9,
  output [31:0] out_10,
  output [31:0] out_11,
  output [31:0] out_12,
  output [31:0] out_13,
  output [31:0] out_14,
  output [31:0] out_15,
  output [31:0] out_16,
  output [31:0] out_17,
  output [31:0] out_18,
  output [31:0] out_19,
  output [31:0] out_20,
  output [31:0] out_21,
  output [31:0] out_22,
  output [31:0] out_23,
  output [31:0] out_24,
  output [31:0] out_25,
  output [31:0] out_26,
  output [31:0] out_27,
  output [31:0] out_28,
  output [31:0] out_29,
  output [31:0] out_30,
  output [31:0] out_31,
  output [31:0] out_32,
  output [31:0] out_33
);


  assign _0 = {32{1'b0}};
  assign out_2 = {32{1'b0}};
  assign out_3 = {32{1'b0}};
  assign out_4 = {32{1'b0}};
  assign out_5 = {32{1'b0}};
  assign out_7 = {32{1'b0}};
  assign out_8 = {32{1'b0}};
  assign out_9 = 32'h1e000;
  assign out_10 = 32'h61000;
  assign out_11 = 32'h1c80800;
  assign out_12 = 32'h2380800;
  assign out_13 = 32'h208c880;
  assign out_14 = 32'h1900740;
  assign out_15 = 32'h600040;
  assign out_16 = 32'h1880040;
  assign out_17 = 32'h2080180;
  assign out_18 = 32'h2160240;
  assign out_19 = 32'h1e10040;
  assign out_20 = 32'h10040;
  assign out_21 = 32'h10080;
  assign out_22 = 32'h8040;
  assign out_23 = 32'h8180;
  assign out_24 = 32'h8040;
  assign out_25 = 32'h8040;
  assign out_26 = 32'h4080;
  assign out_27 = 32'h3f00;
  assign out_28 = {32{1'b0}};
  assign out_29 = {32{1'b0}};
  assign out_30 = {32{1'b0}};
  assign out_31 = {32{1'b0}};
  assign out_32 = {32{1'b0}};
  assign out_33 = {32{1'b0}};
endmodule
